# Fritzing sketch MIX0401_Test (saved by Fritzing 0.9.3b)
breadboards: 1

parts:
  C1 = Electrolytic Capacitor [capacitance=1µF package="100 mil [THT, electrolytic]"]
  C2 = Electrolytic Capacitor [capacitance=1µF package="100 mil [THT, electrolytic]"]
  C3 = Electrolytic Capacitor [capacitance=1µF package="100 mil [THT, electrolytic]"]
  R1 = Resistor [tolerance=±5% resistance=10k package=THT]
  R2 = Resistor [tolerance=±5% resistance=10k package=THT]
  R3 = Resistor [tolerance=±5% resistance=10k package=THT]
  IC1 = Dual Op-Amp [package=dip08]
  R4 = Resistor [tolerance=±5% resistance=2.2k package=THT]
  IC2 = Dual Op-Amp [package=dip08]
  R5 = Resistor [tolerance=±5% resistance=33k package=THT]
  C4 = Ceramic Capacitor [capacitance=100nF package="100 mil [THT, multilayer]"]
  R6 = Resistor [tolerance=±5% resistance=560 package=THT]
  R7 = Rotary Potentiometer (Small) [maximum_resistance=100kΩ package=THT]
  C5 = Electrolytic Capacitor [capacitance=1µF package="100 mil [THT, electrolytic]"]
  R8 = Resistor [tolerance=±5% resistance=100k package=THT]
  C6 = Ceramic Capacitor [capacitance=100nF package="100 mil [THT, multilayer]"]
  C7 = Ceramic Capacitor [capacitance=100nF package="100 mil [THT, multilayer]"]
  C8 = Ceramic Capacitor [capacitance=100nF package="100 mil [THT, multilayer]"]
  C9 = Ceramic Capacitor [capacitance=100nF package="100 mil [THT, multilayer]"]
  C10 = Electrolytic Capacitor [capacitance=1µF package="100 mil [THT, electrolytic]"]
  R9 = Resistor [tolerance=±5% resistance=10k package=THT]
  C11 = Electrolytic Capacitor [capacitance=1µF package="100 mil [THT, electrolytic]"]
  R10 = Resistor [tolerance=±5% resistance=100k package=THT]
  R11 = Resistor [tolerance=±5% resistance=100k package=THT]
  R12 = Rotary Potentiometer (Small) [maximum_resistance=100kΩ package=THT]
  R13 = Rotary Potentiometer (Small) [maximum_resistance=100kΩ package=THT]
  R14 = Rotary Potentiometer (Small) [maximum_resistance=100kΩ package=THT]
  R15 = Rotary Potentiometer (Small) [maximum_resistance=100kΩ package=THT]
  RCA1 = RCA [package=pth]
  RCA2 = RCA [package=pth]
  RCA3 = RCA [package=pth]
  RCA4 = RCA [package=pth]
  C14 = Electrolytic Capacitor [capacitance=1µF package="100 mil [THT, electrolytic]"]
  R16 = Resistor [tolerance=±20% resistance=1k package=THT]
  LED1 = LED - 5mm [color="Green (560nm)" package="5 mm [THT]"]
  R17 = Resistor [tolerance=±5% resistance=100 package=THT]
  Power_plug1 = Power plug
  C15 = Electrolytic Capacitor [capacitance=1µF package="100 mil [THT, electrolytic]"]
  R18 = Resistor [tolerance=±5% resistance=470 package=THT]
  C16 = Film/Foil Capacitor [capacitance=100nF voltage=35V package="5mm [THT, pp]"]

nets:
  N1: C1.-, R12.wiper
  N2: C1.+, R1.Pin_0
  N3: C2.-, R13.wiper
  N4: C2.+, R2.Pin_0
  N5: C3.-, R14.wiper
  N6: C3.+, R3.Pin_0
  N7: R1.Pin_1, R2.Pin_1, R3.Pin_1, IC1.A_-IN, R5.Pin_0, C4.0, R9.Pin_1
  N8: IC1.A_OUT, R5.Pin_1, C4.1, R6.Pin_0
  N9: IC1.A_+IN, R4.Pin_0
  N10: IC1.A_V-, IC2.A_V-, R8.Pin_1, C8.0, C9.1, C11.-, R11.Pin_1, R12.leg1, R13.leg1, R14.leg1, R15.leg1, RCA1.PIN, RCA2.PIN, RCA3.PIN, RCA4.PIN, C14.-, Power_plug1.GND, R18.Pin_1, C16.+
  N11: IC1.B_+IN, R10.Pin_1, R11.Pin_0
  N12: IC1.B_-IN, IC1.B_OUT, R4.Pin_1, IC2.A_+IN, C6.1, C7.0, C8.1, C9.0, C14.+, LED1.cathode, C15.-
  N13: IC1.A_V+, IC2.A_V+, C6.0, C7.1, C11.+, R10.Pin_0, R16.Pin_0, Power_plug1.VCC, C15.+
  N14: IC2.A_OUT, IC2.B_+IN, R7.wiper, R7.leg2
  N15: IC2.A_-IN, R6.Pin_1, R7.leg1
  N16: IC2.B_-IN, IC2.B_OUT, R17.Pin_0
  N17: C5.-, R8.Pin_0, R18.Pin_0, C16.-
  N18: C5.+, R17.Pin_1
  N19: C10.-, R15.wiper
  N20: C10.+, R9.Pin_0
  N21: R12.leg2, RCA1.SHELL
  N22: R13.leg2, RCA2.SHELL
  N23: R14.leg2, RCA3.SHELL
  N24: R15.leg2, RCA4.SHELL
  N25: R16.Pin_1, LED1.anode

notes:
  VCC/2
  VCC
  GND
  VCC/2
  OUT
  IN1
  IN2
  IN3
  IN4
  10k/A x 4
  10k/A
  DC9V IN
