# Fritzing sketch MIX0401_Test_Master (saved by Fritzing 0.9.3b)
breadboards: 1

parts:
  IC1 = Dual Op-Amp [package=dip08]
  R1 = Rotary Potentiometer (Small) [maximum_resistance=100kΩ package=THT]
  R2 = Rotary Potentiometer (Small) [maximum_resistance=100kΩ package=THT]
  C1 = Electrolytic Capacitor [capacitance=1µF package="100 mil [THT, electrolytic]"]
  C2 = Electrolytic Capacitor [capacitance=1µF package="100 mil [THT, electrolytic]"]
  C3 = Electrolytic Capacitor [capacitance=1µF package="100 mil [THT, electrolytic]"]
  C4 = Electrolytic Capacitor [capacitance=1µF package="100 mil [THT, electrolytic]"]
  R8 = Resistor [tolerance=±5% resistance=1.5k package=THT]
  R9 = Resistor [tolerance=±5% resistance=8.2k package=THT]
  R10 = Resistor [tolerance=±5% resistance=1.5k package=THT]
  R11 = Resistor [tolerance=±5% resistance=8.2k package=THT]
  R3 = Resistor [tolerance=±5% resistance=10k package=THT]
  R4 = Resistor [tolerance=±5% resistance=10k package=THT]
  R6 = Resistor [tolerance=±5% resistance=10k package=THT]
  R7 = Resistor [tolerance=±5% resistance=10k package=THT]
  R5 = Resistor [tolerance=±5% resistance=2.2k package=THT]
  R12 = Resistor [tolerance=±5% resistance=33k package=THT]
  C5 = Ceramic Capacitor [capacitance=100nF package="100 mil [THT, multilayer]"]
  C6 = Ceramic Capacitor [capacitance=100nF package="100 mil [THT, multilayer]"]
  C7 = Ceramic Capacitor [capacitance=100nF package="100 mil [THT, multilayer]"]
  IC2 = Dual Op-Amp [package=dip08]
  R14 = Rotary Potentiometer (Small) [maximum_resistance=100kΩ package=THT]
  IC3 = Dual Op-Amp [package=dip08]
  C8 = Ceramic Capacitor [capacitance=100nF package="100 mil [THT, multilayer]"]
  C9 = Ceramic Capacitor [capacitance=100nF package="100 mil [THT, multilayer]"]
  C10 = Ceramic Capacitor [capacitance=100nF package="100 mil [THT, multilayer]"]
  C11 = Ceramic Capacitor [capacitance=100nF package="100 mil [THT, multilayer]"]
  R13 = Resistor [tolerance=±5% resistance=560 package=THT]
  C12 = Electrolytic Capacitor [capacitance=1µF package="100 mil [THT, electrolytic]"]
  R15 = Resistor [tolerance=±5% resistance=1k package=THT]

nets:
  N1: IC1.A_OUT, R12.Pin_0, C5.0, R13.Pin_1
  N2: IC1.A_-IN, R3.Pin_0, R4.Pin_0, R12.Pin_1, C5.1
  N3: IC1.A_+IN, R5.Pin_0
  N4: IC1.A_V-, C7.0, IC2.A_V-, IC3.A_V-, C10.0, C11.0
  N5: IC1.B_+IN, R1.leg1, R2.leg1, R8.Pin_0, R10.Pin_0, R5.Pin_1, C6.0, C7.1, IC2.A_+IN, IC2.B_+IN, IC3.B_+IN, C8.0, C9.0, C10.1, C11.1, R15.Pin_1
  N6: IC1.B_-IN, IC1.B_OUT
  N7: IC1.A_V+, C6.1, IC2.A_V+, IC3.A_V+, C8.1, C9.1
  N8: R1.wiper, C1.+
  N9: R2.wiper, C2.+
  N10: C1.-, R3.Pin_1
  N11: C2.-, R4.Pin_1
  N12: C3.-, R6.Pin_1
  N13: C3.+, R8.Pin_1, R9.Pin_0
  N14: C4.-, R7.Pin_1
  N15: C4.+, R10.Pin_1, R11.Pin_0
  N16: IC2.A_OUT, R14.leg1, IC3.A_+IN
  N17: IC2.A_-IN, R14.wiper, R14.leg2, R13.Pin_0
  N18: IC2.B_-IN, IC2.B_OUT
  N19: IC3.A_-IN, C12.+
  N20: IC3.B_-IN, IC3.B_OUT
  N21: C12.-, R15.Pin_0

notes:
  GND
  +5V
  -5V
  GND
  IN1
  IN2
  IN3
  IN4
  Samming
  Point
  Master
  Out
