# Fritzing sketch MIX0401_ケース内配線図 (saved by Fritzing 0.9.3b)
perfboards: 1

parts:
  RCA1 = RCA [package=pth]
  RCA2 = RCA [package=pth]
  RCA3 = RCA [package=pth]
  RCA4 = RCA [package=pth]
  R1 = Rotary Potentiometer (Small) [maximum_resistance=100kΩ package=THT]
  R2 = Rotary Potentiometer (Small) [maximum_resistance=100kΩ package=THT]
  R3 = Rotary Potentiometer (Small) [maximum_resistance=100kΩ package=THT]
  R4 = Rotary Potentiometer (Small) [maximum_resistance=100kΩ package=THT]
  J1 = female pin header, 5 pins [form="♀ (female)"]
  J2 = female pin header, 2 pins [form="♀ (female)"]
  RCA5 = RCA [package=pth]
  J3 = female pin header, 2 pins [form="♀ (female)"]
  R5 = Rotary Potentiometer (Small) [maximum_resistance=100kΩ package=THT]
  J4 = female pin header, 2 pins [form="♀ (female)"]
  Power_plug1 = Power plug
  S1 = Taiway 100-SP-X-T1 SPDT Miniature Toggle Switch [part_number=100-SP-X-T1-0-0-B1-M1 package=THT]  # not connected

nets:
  N1: RCA1.PIN, R1.leg2
  N2: RCA1.SHELL, RCA2.SHELL, RCA3.SHELL
  N3: RCA2.PIN, R2.leg2
  N4: RCA3.PIN, R3.leg2
  N5: RCA4.PIN, R4.leg2
  N6: R1.leg1, R2.leg1, R3.leg1, R4.leg1, J1.pin5
  N7: R1.wiper, J1.pin1
  N8: R2.wiper, J1.pin2
  N9: R4.wiper, J1.pin4
  N10: J2.pin1, RCA5.SHELL
  N11: J2.pin2, RCA5.PIN
  N12: J3.pin1, R5.leg1
  N13: J3.pin2, R5.wiper, R5.leg2
  N14: J4.pin1, Power_plug1.GND

notes:
  IN1
  IN2
  IN3
  IN4
  OUT
  MASTER
  LEVEL
  PWRIN
  MIX0401 Main board
  PWRSW
